# Fritzing sketch MicrophoneCircuit (saved by Fritzing 0.9.3b)
breadboards: 1

parts:
  Part1 = Arduino Uno (Rev3)
  Part2 = Breakout Board for Electret Microphone
  S1 = Pushbutton [package="[THT]"]

nets:
  N1: Part1.A0, Part2.VCC
  N2: Part1.5V, Part2.AUD
  GND: Part1.GND, Part2.GND
  N3: S1.Pin_1, S1.Pin_2
  N4: S1.Pin_3, S1.Pin_4
